# Fritzing sketch LDR+LED+Buzzer (saved by Fritzing 0.9.3b)
breadboards: 1

parts:
  MH-ET_LIVE_ESP32_DEVKIT1 = MH-ET LIVE ESP32 DEVKIT 38 pins
  LED1 = LED - 3mm [color="Red (633nm)" package="3 mm [THT]"]  # not connected
  J1 = Piezo Speaker
  R2 = Resistor [tolerance=±5% resistance=220 package="0603 [SMD]"]
  R3 = Resistor [tolerance=±5% resistance=220 package="0603 [SMD]"]
  R4 = Photocell (LDR) [package=THT]

nets:
  N1: MH-ET_LIVE_ESP32_DEVKIT1.3V3, R4.pin_0
  N2: MH-ET_LIVE_ESP32_DEVKIT1.IO35, R3.Pin_0, R4.pin_1
  N3: MH-ET_LIVE_ESP32_DEVKIT1.GND#64, J1.pin1, R2.Pin_1, R3.Pin_1
  N4: MH-ET_LIVE_ESP32_DEVKIT1.IO18, J1.pin2

custom parts:
  MH-ET LIVE ESP32 DEVKIT 38 pins: http://mh.nodebb.com/topic/2/mh-et-live-esp32-devkit
