# Fritzing sketch Sensors (saved by Fritzing 0.9.3b)
breadboards: 1

parts:
  SEN1 = Pulse Sensor [package=SIP-3]
  J1 = female pin header, 2 pins [form="♀ (female)"]
  J2 = female pin header, 1 pin [form="♀ (female)"]
  MH-ET_LIVE_ESP32_DEVKIT1 = MH-ET LIVE ESP32 DEVKIT 38 pins
  OLED1 = OLED 128x64 I2C Monochrome Display
  Mod1 = KY-023 Dual Axis Joystick Module [package="Breakout board"]
  Part1 = InvenSense MPU6050
  VCC1 = Battery block 9V
  U1 = Voltage Regulator [package=to220-adj]

nets:
  GND: SEN1.GND, J1.pin1, MH-ET_LIVE_ESP32_DEVKIT1.GND#64, OLED1.GND, Mod1.GND, Part1.GND, VCC1.-, U1.IN
  VCC: SEN1.VCC, J1.pin2, MH-ET_LIVE_ESP32_DEVKIT1.3V3, OLED1.VDD, Mod1.+5V, Part1.VCC
  N1: SEN1.Signal, J2.pin1, MH-ET_LIVE_ESP32_DEVKIT1.IO34
  N2: MH-ET_LIVE_ESP32_DEVKIT1.IO32, Mod1.VRx
  N3: MH-ET_LIVE_ESP32_DEVKIT1.IO33, Mod1.VRy
  N4: MH-ET_LIVE_ESP32_DEVKIT1.IO25, Mod1.SW
  N5: MH-ET_LIVE_ESP32_DEVKIT1.5V, U1.ADJ
  N6: MH-ET_LIVE_ESP32_DEVKIT1.IO22, OLED1.SDA, Part1.SDA
  N7: MH-ET_LIVE_ESP32_DEVKIT1.IO21, OLED1.SCK, Part1.SCL
  N8: VCC1.+, U1.OUT

custom parts:
  Pulse Sensor: Pulse Sensor Optical Heart Beat Sensor
  MH-ET LIVE ESP32 DEVKIT 38 pins: http://mh.nodebb.com/topic/2/mh-et-live-esp32-devkit
  KY-023 Dual Axis Joystick Module: KY-023 Dual-Axis Joystick Module.
